# Fritzing sketch optical (saved by Fritzing 0.9.1b)
breadboards: 1

parts:
  J1 = Piezo Speaker
  R1 = Resistor [tolerance=±5% resistance=10k package=THT]
  R2 = Photocell (LDR) [package=THT]
  元件1 = SunFounder Uno R3

nets:
  N1: J1.pin1, R1.Pin_1, 元件1.GND
  N2: J1.pin2, 元件1.D9_PWM
  N3: R1.Pin_0, R2.pin_1, 元件1.A0
  N4: R2.pin_0, 元件1.5V

custom parts:
  SunFounder Uno R3: The Arduino Uno is a microcontroller board based on the ATmega328 (datasheet). It has 14 digital input/output pins (of which 6 can be used as PWM outputs), 6 analog inputs, a 16 MHz ceramic resonator, a USB connection, a power jack, an ICSP header, and a reset button. It contains everything needed to support the microcontroller; simply connect it to a computer with a USB cable or power it with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
