# Fritzing sketch LM35 Temperature Sensor (saved by Fritzing 0.9.1b)
breadboards: 1

parts:
  module1 = I2C LCD1602
  T1 = LM35 Temperature Sensor [package="TO92 [THT]"]
  元件1 = SunFounder Uno R3

nets:
  N1: module1.SCL, 元件1.A5/SCL
  N2: module1.SDA, 元件1.A4/SDA
  VCC: module1.VCC, T1.+Vs, 元件1.5V
  GND: module1.GND, T1.GND, 元件1.GND
  N3: T1.Vout, 元件1.A0

notes:
  I2C LCD1602

custom parts:
  I2C LCD1602: I2C LCD1602 module of SunFounder Sensor Kit
  SunFounder Uno R3: The Arduino Uno is a microcontroller board based on the ATmega328 (datasheet). It has 14 digital input/output pins (of which 6 can be used as PWM outputs), 6 analog inputs, a 16 MHz ceramic resonator, a USB connection, a power jack, an ICSP header, and a reset button. It contains everything needed to support the microcontroller; simply connect it to a computer with a USB cable or power it with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
