# Fritzing sketch stopwatah (saved by Fritzing 0.9.1b)
breadboards: 1

parts:
  R1 = Resistor [tolerance=±5% resistance=220 package=THT]
  R2 = Resistor [tolerance=±5% resistance=220 package=THT]
  R3 = Resistor [tolerance=±5% resistance=220 package=THT]
  R4 = Resistor [tolerance=±5% resistance=220 package=THT]
  R5 = Resistor [tolerance=±5% resistance=220 package=THT]
  R6 = Resistor [tolerance=±5% resistance=220 package=THT]
  R7 = Resistor [tolerance=±5% resistance=220 package=THT]
  R8 = Resistor [tolerance=±5% resistance=220 package=THT]
  元件1 = SunFounder Uno R3
  LED2 = 7-SEGMENT-4DIGIT-YOUNGSUN [package=7-segment-4digit-youngsun-longpads]

nets:
  N1: R1.Pin_0, LED2.APOS-A
  N2: R1.Pin_1, 元件1.D3_PWM
  N3: R2.Pin_0, 元件1.D7
  N4: R2.Pin_1, LED2.C
  N5: R3.Pin_0, 元件1.D2
  N6: R3.Pin_1, LED2.A
  N7: R4.Pin_0, 元件1.D6_PWM
  N8: R4.Pin_1, LED2.DIG2
  N9: R5.Pin_0, 元件1.D5_PWM
  N10: R5.Pin_1, LED2.D
  N11: R6.Pin_0, LED2.E
  N12: R6.Pin_1, 元件1.D4
  N13: R7.Pin_0, LED2.COL-A
  N14: R7.Pin_1, 元件1.D9_PWM
  N15: R8.Pin_0, LED2.DIG3
  N16: R8.Pin_1, 元件1.D8
  N17: 元件1.ICSP_MISO, 元件1.D12/MISO, LED2.COL-C
  N18: 元件1.ICSP_MOSI, 元件1.D11_PWM/MOSI, LED2.F
  N19: 元件1.D10_PWM/SS, LED2.DP
  N20: 元件1.D13/SCK, LED2.G

custom parts:
  SunFounder Uno R3: The Arduino Uno is a microcontroller board based on the ATmega328 (datasheet). It has 14 digital input/output pins (of which 6 can be used as PWM outputs), 6 analog inputs, a 16 MHz ceramic resonator, a USB connection, a power jack, an ICSP header, and a reset button. It contains everything needed to support the microcontroller; simply connect it to a computer with a USB cable or power it with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
  7-SEGMENT-4DIGIT-YOUNGSUN: This is a part for the 4-Digit 7-segment LEDs from Young Sun. Different from the Digikey LEDs, all 16 pins are used. The LONGPADS Variant is used for a test jig, but you may like it because there is more pad to solder to. If you are concerned about routing space, the standard works just fine though.
