# Fritzing sketch step motor (saved by Fritzing 0.9.1b)

parts:
  module2 = Stepper Motor Driver
  module3 = Step Motor
  元件1 = SunFounder Uno R3

nets:
  N1: module2.D, 元件1.ICSP_MOSI, 元件1.D11_PWM/MOSI
  N2: module2.C, 元件1.D10_PWM/SS
  N3: module2.B, 元件1.D9_PWM
  N4: module2.A, 元件1.D8
  N5: module2.OUT1, module3.blue
  VCC: module2.VCC, 元件1.5V
  GND: module2.GND, 元件1.GND
  N6: module2.OUT2, module3.pink
  N7: module2.OUT3, module3.yellow
  N8: module2.OUT4, module3.orange
  N9: module2.COM, module3.red

custom parts:
  Stepper Motor Driver: Stepper Motor Driver of SunFounder Sensor Kit for Arduino
  Step Motor: step motor
  SunFounder Uno R3: The Arduino Uno is a microcontroller board based on the ATmega328 (datasheet). It has 14 digital input/output pins (of which 6 can be used as PWM outputs), 6 analog inputs, a 16 MHz ceramic resonator, a USB connection, a power jack, an ICSP header, and a reset button. It contains everything needed to support the microcontroller; simply connect it to a computer with a USB cable or power it with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
