# Fritzing sketch Controlling LED by PWM (saved by Fritzing 0.8.7b)
breadboards: 1

parts:
  LED1 = smd LED [color="Red (635nm)" package="0603 [SMD]"]
  元件1 = SunFounder Uno R3
  R1 = Resistor [tolerance=±5% resistance=220 package=THT]

nets:
  N1: LED1.cathode, 元件1.GND
  N2: 元件1.D9_PWM, R1.Pin_1

custom parts:
  SunFounder Uno R3: The Arduino Uno is a microcontroller board based on the ATmega328 (datasheet). It has 14 digital input/output pins (of which 6 can be used as PWM outputs), 6 analog inputs, a 16 MHz ceramic resonator, a USB connection, a power jack, an ICSP header, and a reset button. It contains everything needed to support the microcontroller; simply connect it to a computer with a USB cable or power it with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
