# Fritzing sketch Infrared-Receiver (saved by Fritzing 0.9.1b)
breadboards: 1

parts:
  module2 = Infrared-Receiver
  R1 = Resistor [tolerance=±5% resistance=220 package=THT]
  LED1 = LED - 5mm [color="Red (633nm)" package="5 mm [THT]"]
  元件1 = SunFounder Uno R3

nets:
  N1: module2.SIG, 元件1.D7
  GND: module2.GND, LED1.cathode, 元件1.GND
  VCC: module2.VCC, 元件1.5V
  N2: R1.Pin_0, LED1.anode
  N3: R1.Pin_1, 元件1.D13/SCK

notes:
  Infrared-Receiver

custom parts:
  Infrared-Receiver: Infrared-Receiver module of SunFounder Sensor Kit
  SunFounder Uno R3: The Arduino Uno is a microcontroller board based on the ATmega328 (datasheet). It has 14 digital input/output pins (of which 6 can be used as PWM outputs), 6 analog inputs, a 16 MHz ceramic resonator, a USB connection, a power jack, an ICSP header, and a reset button. It contains everything needed to support the microcontroller; simply connect it to a computer with a USB cable or power it with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
