# Fritzing sketch I2C_LCD1602 (saved by Fritzing 0.9.1b)

parts:
  I2C_LCD1602 = I2C LCD1602
  元件1 = SunFounder Uno R3

nets:
  N1: I2C_LCD1602.SCL, 元件1.A5/SCL
  N2: I2C_LCD1602.SDA, 元件1.A4/SDA
  VCC: I2C_LCD1602.VCC, 元件1.5V
  GND: I2C_LCD1602.GND, 元件1.GND

custom parts:
  I2C LCD1602: I2C LCD1602 module of SunFounder Sensor Kit
  SunFounder Uno R3: The SunFounder Uno is a microcontroller board based on the ATmega328 (datasheet). It has 14 digital input/output pins (of which 6 can be used as PWM outputs), 6 analog inputs, a 16 MHz ceramic resonator, a USB connection, a power jack, an ICSP header, and a reset button. It contains everything needed to support the microcontroller; simply connect it to a computer with a USB cable or power it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
