# Fritzing sketch Tilt_Switch (saved by Fritzing 0.9.1b)

parts:
  元件1 = SunFounder Uno R3
  S1 = Tilt Switch [package=THT]

nets:
  N1: 元件1.GND, S1.Pin_1
  N2: 元件1.D2, S1.Pin_2

custom parts:
  SunFounder Uno R3: The Arduino Uno is a microcontroller board based on the ATmega328 (datasheet). It has 14 digital input/output pins (of which 6 can be used as PWM outputs), 6 analog inputs, a 16 MHz ceramic resonator, a USB connection, a power jack, an ICSP header, and a reset button. It contains everything needed to support the microcontroller; simply connect it to a computer with a USB cable or power it with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
