# Fritzing sketch Building a Quiz Buzzer System (saved by Fritzing 0.9.1b)
breadboards: 1

parts:
  S1 = Pushbutton [package="[THT]"]
  S2 = Pushbutton [package="[THT]"]
  S3 = Pushbutton [package="[THT]"]
  S4 = Pushbutton [package="[THT]"]
  LED2 = LED - 5mm [color="Red (633nm)" package="5 mm [THT]"]
  LED3 = LED - 5mm [color="Red (633nm)" package="5 mm [THT]"]
  LED4 = LED - 5mm [color="Red (633nm)" package="5 mm [THT]"]
  R1 = Resistor [tolerance=±5% resistance=220 package=THT]
  R2 = Resistor [tolerance=±5% resistance=220 package=THT]
  R3 = Resistor [tolerance=±5% resistance=220 package=THT]
  R4 = Resistor [tolerance=±5% resistance=220 package=THT]
  J1 = Piezo Speaker
  LED1 = smd LED [color="Red (633nm)" package="0805 [SMD]"]
  LED1_2 = smd LED [color="Red (633nm)" package="1206 [SMD]"]
  元件1 = SunFounder Uno R3

nets:
  N1: S1.Pin_1, S1.Pin_2, 元件1.D4
  N2: S1.Pin_3, S1.Pin_4, S2.Pin_1, S2.Pin_2, S3.Pin_1, S3.Pin_2, S4.Pin_3, S4.Pin_4, LED2.cathode, LED3.cathode, LED4.cathode, J1.pin1, LED1.cathode, LED1_2.cathode, 元件1.GND
  N3: S2.Pin_3, S2.Pin_4, 元件1.D2
  N4: S3.Pin_3, S3.Pin_4, 元件1.D3_PWM
  N5: S4.Pin_1, S4.Pin_2, 元件1.D9_PWM
  N6: LED2.anode, R4.Pin_1
  N7: LED3.anode, R1.Pin_1
  N8: LED4.anode, R3.Pin_1
  N9: R1.Pin_0, 元件1.D10_PWM/SS
  N10: R2.Pin_0, 元件1.D7
  N11: R2.Pin_1, LED1.anode, LED1_2.anode
  N12: R3.Pin_0, 元件1.D6_PWM
  N13: R4.Pin_0, 元件1.D8
  N14: J1.pin2, 元件1.D5_PWM

custom parts:
  SunFounder Uno R3: The Arduino Uno is a microcontroller board based on the ATmega328 (datasheet). It has 14 digital input/output pins (of which 6 can be used as PWM outputs), 6 analog inputs, a 16 MHz ceramic resonator, a USB connection, a power jack, an ICSP header, and a reset button. It contains everything needed to support the microcontroller; simply connect it to a computer with a USB cable or power it with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
