# Fritzing sketch photocell (saved by Fritzing 0.9.1b)
breadboards: 1

parts:
  LED2 = LED - 5mm [color="Red (633nm)" package="5 mm [THT]"]
  R4 = Resistor [tolerance=±5% resistance=220 package=THT]
  R5 = Photocell (LDR) [package=THT]
  R6 = Resistor [tolerance=±5% resistance=10k package=THT]
  LED3 = LED - 5mm [color="Red (633nm)" package="5 mm [THT]"]
  LED4 = LED - 5mm [color="Yellow (592nm)" package="5 mm [THT]"]
  LED5 = LED - 5mm [color="Red (633nm)" package="5 mm [THT]"]
  LED6 = LED - 5mm [color="Green (565nm)" package="5 mm [THT]"]
  LED7 = LED - 5mm [color="Yellow (592nm)" package="5 mm [THT]"]
  LED8 = LED - 5mm [color="Green (565nm)" package="5 mm [THT]"]
  R7 = Resistor [tolerance=±5% resistance=220 package=THT]
  R8 = Resistor [tolerance=±5% resistance=220 package=THT]
  R9 = Resistor [tolerance=±5% resistance=220 package=THT]
  R10 = Resistor [tolerance=±5% resistance=220 package=THT]
  R11 = Resistor [tolerance=±5% resistance=220 package=THT]
  R12 = Resistor [tolerance=±5% resistance=220 package=THT]
  R13 = Resistor [tolerance=±5% resistance=220 package=THT]
  LED9 = LED - 5mm [color="Red (633nm)" package="5 mm [THT]"]
  元件1 = SunFounder Uno R3

nets:
  N1: LED2.cathode, R6.Pin_1, LED3.cathode, LED4.cathode, LED5.cathode, LED6.cathode, LED7.cathode, LED8.cathode, LED9.cathode, 元件1.GND
  N2: LED2.anode, R4.Pin_1
  N3: R4.Pin_0, 元件1.D12/MISO
  N4: R5.pin_0, 元件1.5V
  N5: R5.pin_1, R6.Pin_0, 元件1.A0
  N6: LED3.anode, R7.Pin_1
  N7: LED4.anode, R9.Pin_1
  N8: LED5.anode, R12.Pin_1
  N9: LED6.anode, R11.Pin_1
  N10: LED7.anode, R8.Pin_1
  N11: LED8.anode, R10.Pin_1
  N12: R7.Pin_0, 元件1.D11_PWM/MOSI
  N13: R8.Pin_0, 元件1.D10_PWM/SS
  N14: R9.Pin_0, 元件1.D9_PWM
  N15: R10.Pin_0, 元件1.D8
  N16: R11.Pin_0, 元件1.D7
  N17: R12.Pin_0, 元件1.D6_PWM
  N18: R13.Pin_0, 元件1.D5_PWM
  N19: R13.Pin_1, LED9.anode

custom parts:
  SunFounder Uno R3: The Arduino Uno is a microcontroller board based on the ATmega328 (datasheet). It has 14 digital input/output pins (of which 6 can be used as PWM outputs), 6 analog inputs, a 16 MHz ceramic resonator, a USB connection, a power jack, an ICSP header, and a reset button. It contains everything needed to support the microcontroller; simply connect it to a computer with a USB cable or power it with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
